// Logisim project 1612x_MicroProcessor.circ as structural Verilog: 16 circuits, main circuit AR
module Main (
  input  AR_CLR,
  input  PC_CLR,
  input  DR_CLR,
  input  STARTING_PULSE,
  input  IR_CLR,
  input  IR_INR,
  input  TR_LD,
  input  TR_CLR,
  input  TR_INR,
  output [15:0] out_10,
  output [15:0] out_11,
  output [15:0] out_12,
  output [15:0] out_13,
  output [15:0] out_14,
  output out_15,
  output [15:0] out_16,
  output [15:0] out_17,
  output [11:0] out_18
);

  wire AC_CLR, AC_INC, AC_LD, AC_OP_ZERO, ADD, ALU_S0, ALU_S1, ALU_S2, and_1_out, and_2_out, and_6_out,
       and_7_out, and_9_out, and_10_out, and_11_out, and_12_out, and_13_out, and_14_out, and_15_out,
       and_16_out, and_17_out, and_18_out, and_19_out, and_20_out, and_22_out, and_23_out, and_24_out,
       and_25_out, and_26_out, and_28_out, AND_OUT, AR_INC, AR_LD, B0, B1, B2, B3, B4, B5, B6, B7, B8, B9,
       B10, B11, CLK, D0, D1, D2, D3, D4, D5, D6, D7, DR, DR_INC, DR_LD, DR_OP_ZERO, E_CLR, E_CMP, E_LD, I,
       IR_LD, MX_S0, MX_S1, MX_S2, not_1_out, not_2_out, not_3_out, not_5_out, or_1_out, or_2_out, or_11_out,
       or_12_out, or_13_out, PC_INC, PC_LD, R, r_t, rB0, rB1, rB2, rB3, rB4, rB6, rB7, rB9, READ, SC_CLR,
       SC_INC, T0, T2, T3, T4, T5, T6, T7, T8, T9, T10, T11, T12, T13, T14, T15, WRITE;
  wire [15:0] INP_OP, OPR_OP, TR_OP;

  not not_1 (not_1_out, D7);
  and and_1 (and_1_out, D4, T4);
  and and_2 (and_2_out, D5, T5);
  or or_1 (or_1_out, D0, D1, D2, D6);
  and and_3 (AND_OUT, D0, T5);
  and and_4 (ADD, D1, T5);
  and and_5 (DR, D2, T5);
  not not_2 (not_2_out, D7);
  or or_2 (or_2_out, D0, D1, D2, D6);
  and and_6 (and_6_out, D1, T5);
  and and_7 (and_7_out, not_1_out, I, T3);
  or or_3 (PC_LD, and_1_out, and_2_out);
  and and_8 (DR_LD, or_1_out, T4);
  and and_9 (and_9_out, not_2_out, I, T3);
  and and_10 (and_10_out, or_2_out, T4);
  or or_4 (E_LD, and_6_out, rB7, rB6);
  or or_5 (AR_LD, T0, T2, and_7_out);
  or or_6 (AC_LD, AND_OUT, ADD, DR, rB9, rB7, rB6);
  or or_7 (READ, IR_LD, and_9_out, and_10_out);
  Data_Line data_line_1 (
    .MX_S0(MX_S0), .MX_S1(MX_S1), .MX_S2(MX_S2), .MEM_OUT(out_16), .AR_INC(AR_INC), .AR_LOAD(AR_LD),
    .AR_CLEAR(AR_CLR), .PC_INC(PC_INC), .PC_LOAD(PC_LD), .PC_CLEAR(PC_CLR), .E_COMP(E_CMP), .E_CLR(E_CLR),
    .DR_INC(DR_INC), .DR_LOAD(DR_LD), .E_LOAD(E_LD), .DR_CLEAR(DR_CLR), .AC_INC(AC_INC), .AC_LOAD(AC_LD),
    .AC_CLEAR(AC_CLR), .rB6(rB6), .rB7(rB7), .ADD(ADD), .ALU_S0(ALU_S0), .ALU_S1(ALU_S1), .ALU_S2(ALU_S2),
    .IR_LOAD(IR_LD), .TR_INC(TR_INR), .TR_LOAD(TR_LD), .TR_CLEAR(TR_CLR), .OP_LOAD(1'b0), .CLK(CLK),
    .ADDRESS(out_18), .MEM_IN(out_17), .AR_OP(out_10), .PC_OP(out_11), .E_op(out_15), .DR_OP(out_12),
    .AC_OP(out_13), .INR_OP(INP_OP), .IR_OP(out_14), .TR_OP(TR_OP), .OPR_OP(OPR_OP));
  and and_11 (and_11_out, D0, T5);
  and and_12 (and_12_out, D1, T5);
  and and_13 (and_13_out, D2, T5);
  and and_14 (and_14_out, D5, T5);
  and and_15 (and_15_out, D3, T4);
  and and_16 (and_16_out, D4, T4);
  and and_17 (and_17_out, D6, T6);
  not not_3 (not_3_out, out_13[15]);
  and and_18 (and_18_out, D3, T4);
  and and_19 (and_19_out, T4, D5);
  and and_20 (and_20_out, D6, T6);
  Timing_Gen timing_gen_1 (
    .IR_OUT(out_14), .IR_DEC_ENABLE(1'b1), .SC_INC(SC_INC), .IFF_CNTRL(1'b1), .SC_CLR(SC_CLR), .SC_EN(1'b1),
    .SC_CLK(CLK), .IFF_CLK(CLK), .T0(T0), .T3(T3), .T1(IR_LD), .B0(B0), .T2(T2), .B1(B1), .T7(T7), .D0(D0),
    .B2(B2), .T4(T4), .T8(T8), .B3(B3), .D1(D1), .T5(T5), .T9(T9), .B4(B4), .D2(D2), .T6(T6), .T10(T10),
    .B5(B5), .D3(D3), .T11(T11), .B6(B6), .D4(D4), .T12(T12), .B7(B7), .D5(D5), .B8(B8), .T13(T13), .B9(B9),
    .D6(D6), .T14(T14), .B10(B10), .D7(D7), .B11(B11), .T15(T15), .IFF_OP(I), .r(r_t), .rB11(AC_CLR),
    .rB10(E_CLR), .rB9(rB9), .rB8(E_CMP), .rB7(rB7), .rB6(rB6), .rB5(AC_INC), .rB4(rB4), .rB3(rB3),
    .rB2(rB2), .rB1(rB1), .rB0(rB0));
  and and_21 (AR_INC, D5, T4);
  and and_22 (and_22_out, D6, T6, DR_OP_ZERO);
  and and_23 (and_23_out, rB4, not_3_out);
  and and_24 (and_24_out, rB3, out_13[15]);
  and and_25 (and_25_out, rB2, AC_OP_ZERO);
  and and_26 (and_26_out, rB1, out_15);
  and and_27 (DR_INC, D6, T5);
  or or_8 (WRITE, and_18_out, and_19_out, and_20_out);
  or or_9 (SC_CLR, and_11_out, and_12_out, and_13_out, and_14_out, and_16_out, and_17_out, r_t, and_15_out);
  or or_10 (PC_INC, IR_LD, and_22_out, and_23_out, and_24_out, and_25_out, and_26_out);
  RAM #(.addrWidth(12), .asyncread("true"), .dataWidth(16)) ram_1 (
    .addr(out_18), .we(WRITE), .oe(READ), .clk(CLK), .din(out_17), .dout(out_16));
  or or_11 (or_11_out, out_13[15], out_13[14], out_13[13], out_13[12], out_13[11], out_13[10], out_13[9], out_13[8], out_13[7], out_13[6], out_13[5], out_13[4], out_13[3], out_13[2], out_13[1], out_13[0]);
  not not_4 (AC_OP_ZERO, or_11_out);
  not not_5 (not_5_out, rB0);
  or or_12 (or_12_out, out_12[15], out_12[14], out_12[13], out_12[12], out_12[11], out_12[10], out_12[9], out_12[8], out_12[7], out_12[6], out_12[5], out_12[4], out_12[3], out_12[2], out_12[1], out_12[0]);
  MUX_SELECT mux_select_1 (
    .D4(D4), .T4(T4), .D5(D5), .T5(T5), .D6(D6), .T6(T6), .D3(D3), .T2(T2), .T0(T0), .D1(D1), .D2(D2),
    .D0(D0), .D7(D7), .I(I), .T3(T3), .T1(IR_LD), .R(R), .S0(MX_S0), .S1(MX_S1), .S2(MX_S2));
  ALU_SELECT alu_select_1 (
    .IFF(I), .B9(B9), .D5(D5), .T5(T5), .D6(D6), .D7(D7), .T3(T3), .D1(D1), .D2(D2), .D0(D0),
    .ALU_S0(ALU_S0), .ALU_S1(ALU_S1), .ALU_S2(ALU_S2));
  // Probe on out_15
  and and_28 (and_28_out, not_5_out, SC_INC);
  Clock MASTER_CLK (.out(CLK));
  not not_6 (DR_OP_ZERO, or_12_out);
  // Probe on out_10
  // Probe on out_11
  // Probe on out_12
  // Probe on out_13
  // Probe on out_14
  // Probe on out_16
  // Probe on out_17
  // Probe on out_18
  D_Flip_Flop d_ff_1 (.D(or_13_out), .clk(CLK), .Q(SC_INC));  // open: Qn, preset, reset
  or or_13 (or_13_out, STARTING_PULSE, and_28_out);

  // Other names for the same wires on the sheet: AC_OP[15:0] = out_13; AC_15 = out_13[15]; ADDRESS[11:0] = out_18;
  //   AR_OP[15:0] = out_10; DR_OP[15:0] = out_12; E_OP = out_15; IR_INC = IR_INR; IR_OP[15:0] = out_14;
  //   M_IN[15:0] = out_17; MEM_OUT[15:0] = out_16; PC_OP[15:0] = out_11; rB5 = AC_INC; rB8 = E_CMP; rB10 = E_CLR;
  //   rB11 = AC_CLR; T1 = IR_LD; TR_INC = TR_INR

  // Notes on the sheet:
  //   MAIN CIRCUIT
  //   ----- AC LOGIC -----
  //   AC LOAD
  //   ----- IR LOGIC -----
  //   ----- SC LOGIC -----
  //   E LOAD
  //   ----- AR LOGIC -----
  //   AR LOAD
  //   ----- PC LOGIC -----
  //   PC LOAD
  //   ----- DR LOGIC -----
  //   DR LOAD
  //   IR LOAD
  //   ----- TR LOGIC -----
  //   TR LOAD
  //   ----- MEMORY LOGIC -----
  //   MEMORY READ
  //   ----- EFF LOGIC  -----
  //   ----- SUBCIRCUIT INTEGRATION -----
  //   PC CLR
  //   AC CLR
  //   IR CLR
  //   TR CLR
  //   E CLR
  //   AR CLR
  //   DR CLR
  //   SC CLR
  //   PC INR
  //   AC INR
  //   IR INR
  //   TR INR
  //   AR INC
  //   DR INR
  //   MEMORY WRITE
  //   E CMP
  //   ----- MEMORY -----
  //   ----- EXTRA -----
  //   ----- MUX SELECTION -----
  //   ----- ALU SELECTION -----
  //   ----- OUTPUT PANNEL -----
  //   ----- START STOP PULSE GENERATION -----
  //   ----- MASTER CLOCK -----
endmodule

module ALU_16bit (
  input  [15:0] DR,
  input  [15:0] INPR,
  input  [15:0] AC,
  input  S0,
  input  S1,
  input  S2,
  input  [15:0] SHR,
  input  [15:0] SHL,
  output ALU_0,
  output Cout,
  output ALU_15,
  output [15:0] OP
);

  wire [15:0] adder_1_out, and_1_out, not_1_out;

  assign and_1_out = DR & AC;  // AND_Gate and_1, 16 bits wide
  Adder #(.width(16)) adder_1 (.a(DR), .b(AC), .out(adder_1_out), .cin(1'b0), .cout(Cout));
  assign not_1_out = ~AC;  // NOT_Gate not_1, 16 bits wide
  Multiplexer #(.select(3), .width(16)) multiplexer_1 (
    .in0({16{1'b0}}), .in1(and_1_out), .in2(adder_1_out), .in3(DR), .in4(INPR), .in5(not_1_out),
    .in6({1'b0, SHR[15:1]}), .in7({SHL[14:0], 1'b0}), .out({ALU_15, OP[14:1], ALU_0}), .sel({S2, S1, S0}));

  assign {OP[15], OP[0]} = {ALU_15, ALU_0};

  // Notes on the sheet:
  //   USE - 
  //   ARITHMETIC LOGIC UNIT (ALU)
  //   as logical operations like AND, OR, NOT, and XOR.
  //   The Arithmetic Logic Unit (ALU) is a critical component of the CPU that performs arithmetic and logical
  //   operations. It carries out basic operations such as addition, subtraction, multiplication, and division, as well
endmodule

module E_FF (
  input  CMP,
  input  CLR,
  input  INP,
  input  Load,
  input  CLK,
  output OP
);

  wire multiplexer_1_out, multiplexer_2_out, multiplexer_3_out, not_1_out;

  not not_1 (not_1_out, OP);
  Multiplexer multiplexer_1 (.in0(OP), .in1(not_1_out), .out(multiplexer_1_out), .sel(CMP));
  Multiplexer multiplexer_2 (.in0(multiplexer_1_out), .in1(1'b0), .out(multiplexer_2_out), .sel(CLR));
  Multiplexer multiplexer_3 (.in0(multiplexer_2_out), .in1(INP), .out(multiplexer_3_out), .sel(Load));
  D_Flip_Flop d_ff_1 (.D(multiplexer_3_out), .clk(CLK), .Q(OP));  // open: Qn, preset, reset

  // Notes on the sheet:
  //   USE - 
  //   E FLIP FLOP
  //   basic memory element that holds a bit of data until it is updated. 
  //   The E flip-flop (Enable flip-flop) is used to store and control the flow of data in digital circuits. It acts as a
endmodule

module SEQ_COUNTER (
  input  INC,
  input  CLEAR,
  input  SC_Enable,
  input  CLK,
  output [15:0] OP
);

  wire [3:0] adder_1_out, multiplexer_1_out, multiplexer_2_out, register_1_q;

  Adder #(.width(4)) adder_1 (.a(register_1_q), .b(4'b0001), .out(adder_1_out));  // open: cin, cout
  Multiplexer #(.width(4)) multiplexer_1 (.in0(register_1_q), .in1(adder_1_out), .out(multiplexer_1_out), .sel(INC));
  Multiplexer #(.width(4)) multiplexer_2 (.in0(multiplexer_1_out), .in1(4'b0000), .out(multiplexer_2_out), .sel(CLEAR));
  Register #(.width(4)) register_1 (.D(multiplexer_2_out), .clk(CLK), .Q(register_1_q));  // open: en, clr
  Decoder #(.select(4)) decoder_1 (
    .out0(OP[0]), .out1(OP[1]), .out2(OP[2]), .out3(OP[3]), .out4(OP[4]), .out5(OP[5]), .out6(OP[6]),
    .out7(OP[7]), .out8(OP[8]), .out9(OP[9]), .out10(OP[10]), .out11(OP[11]), .out12(OP[12]), .out13(OP[13]),
    .out14(OP[14]), .out15(OP[15]), .sel(register_1_q), .en(SC_Enable));

  // Notes on the sheet:
  //   USE - 
  //   SEQUENCE COUNTER
  //    like T0 to T15
  //   The sequence counter is a vital component in the control unit of a CPU, responsible for generating a series
  //   of timing signals that synchronize the various stages of the instruction cycle. It typically produces signals
endmodule

module Timing_Gen (
  input  [15:0] IR_OUT,
  input  IR_DEC_ENABLE,
  input  SC_INC,
  input  IFF_CNTRL,
  input  SC_CLR,
  input  SC_EN,
  input  SC_CLK,
  input  IFF_CLK,
  output T0,
  output T3,
  output T1,
  output B0,
  output T2,
  output B1,
  output T7,
  output D0,
  output B2,
  output T4,
  output T8,
  output B3,
  output D1,
  output T5,
  output T9,
  output B4,
  output D2,
  output T6,
  output T10,
  output B5,
  output D3,
  output T11,
  output B6,
  output D4,
  output T12,
  output B7,
  output D5,
  output B8,
  output T13,
  output B9,
  output D6,
  output T14,
  output B10,
  output D7,
  output B11,
  output T15,
  output IFF_OP,
  output r,
  output rB11,
  output rB10,
  output rB9,
  output rB8,
  output rB7,
  output rB6,
  output rB5,
  output rB4,
  output rB3,
  output rB2,
  output rB1,
  output rB0
);

  wire multiplexer_1_out, not_1_out;

  not not_1 (not_1_out, IFF_OP);
  SEQ_COUNTER seq_counter_1 (
    .INC(SC_INC), .CLEAR(SC_CLR), .SC_Enable(SC_EN), .CLK(SC_CLK),
    .OP({T15, T14, T13, T12, T11, T10, T9, T8, T7, T6, T5, T4, T3, T2, T1, T0}));
  and and_1 (r, T3, not_1_out, D7);
  and and_2 (rB11, r, IR_OUT[11]);
  and and_3 (rB10, r, IR_OUT[10]);
  and and_4 (rB9, r, IR_OUT[9]);
  and and_5 (rB8, r, IR_OUT[8]);
  and and_6 (rB7, r, IR_OUT[7]);
  and and_7 (rB6, r, IR_OUT[6]);
  and and_8 (rB5, r, IR_OUT[5]);
  and and_9 (rB4, r, IR_OUT[4]);
  and and_10 (rB3, r, IR_OUT[3]);
  and and_11 (rB2, r, IR_OUT[2]);
  and and_12 (rB1, r, IR_OUT[1]);
  and and_13 (rB0, r, IR_OUT[0]);
  Multiplexer multiplexer_1 (.in0(IFF_OP), .in1(IR_OUT[15]), .out(multiplexer_1_out), .sel(IFF_CNTRL));
  D_Flip_Flop d_ff_1 (.D(multiplexer_1_out), .clk(IFF_CLK), .Q(IFF_OP));  // open: Qn, preset, reset
  Decoder #(.select(3)) decoder_1 (
    .out0(D0), .out1(D1), .out2(D2), .out3(D3), .out4(D4), .out5(D5), .out6(D6), .out7(D7),
    .sel(IR_OUT[14:12]), .en(IR_DEC_ENABLE));

  assign B0 = IR_OUT[0];
  assign B1 = IR_OUT[1];
  assign B2 = IR_OUT[2];
  assign B3 = IR_OUT[3];
  assign B4 = IR_OUT[4];
  assign B5 = IR_OUT[5];
  assign B6 = IR_OUT[6];
  assign B7 = IR_OUT[7];
  assign B8 = IR_OUT[8];
  assign B9 = IR_OUT[9];
  assign B10 = IR_OUT[10];
  assign B11 = IR_OUT[11];

  // Other names for the same wires on the sheet: I = IFF_OP

  // Notes on the sheet:
  //   USE - 
  //   TIMING SIGNAL GENERATION SUBCIRCUIT
  //   ----- T Signal Generator -----
  //   ----- Register Reference Signal Generator -----
  //   This sub-circuit generates all required timing signals using a sequence counter, , I Flip Flop and decoders 
  //   ----- B Signal Generator -----
  //   <----- i Flip Flop
  //   ----- D Signal Generator -----
endmodule

module MUX_SELECT (
  input  D4,
  input  T4,
  input  D5,
  input  T5,
  input  D6,
  input  T6,
  input  D3,
  input  T2,
  input  T0,
  input  D1,
  input  D2,
  input  D0,
  input  D7,
  input  I,
  input  T3,
  input  T1,
  input  R,
  output S0,
  output S1,
  output S2
);

  wire and_1_out, and_2_out, and_5_out, and_6_out, and_7_out, and_8_out, and_9_out, not_1_out, not_2_out,
       or_6_out, or_7_out, X1, X2, X3, X4, X6, X7;

  and and_1 (and_1_out, D4, T4);
  and and_2 (and_2_out, D5, T5);
  or or_1 (X1, and_1_out, and_2_out);
  and and_3 (X4, D3, T4);
  not not_1 (not_1_out, R);
  and and_4 (X6, not_1_out, T1);
  and and_5 (and_5_out, D5, T4);
  or or_2 (X2, T0, and_5_out);
  or or_3 (S0, X1, X3, T2, X7);
  or or_4 (S1, X2, X3, X6, X7);
  or or_5 (S2, X4, T2, X6, X7);
  or or_6 (or_6_out, D0, D1, D2);
  not not_2 (not_2_out, D7);
  or or_7 (or_7_out, D0, D1, D2, D6);
  and and_6 (and_6_out, or_6_out, T5);
  and and_7 (and_7_out, D6, T6);
  and and_8 (and_8_out, not_2_out, I, T3);
  and and_9 (and_9_out, or_7_out, T4);
  or or_8 (X3, and_6_out, and_7_out);
  or or_9 (X7, T1, and_8_out, and_9_out);

  // Other names for the same wires on the sheet: X5 = T2

  // Notes on the sheet:
  //   USE - 
  //   ----- AR AS SOURCE -----
  //   ----- AC AS SOURCE -----
  //   ----- TR AS SOURCE -----
  //   AR
  //   PC
  //   DR
  //   AC
  //   IR
  //   TR
  //   MEMORY
  //   (INTERUPT RELATED REGISTER (NOT USED IN CPU)
  //   MUX SELECTION SUBCIRCUIT
  //   ----- PC AS SOURCE -----
  //   ----- IR AS SOURCE -----
  //   appropriate input is selected for execution at each stage of the CPU's operation.
  //   This sub-circuit generates MUX selection signals based on the timing signal, controlling which input is
  //   passed through the MUX for processing. The timing signal synchronizes this process, ensuring that the
  //   routed through the Multiplexer (MUX). These selection signals ensure that the correct data path is chosen at
  //   the right moment in the instruction cycle, allowing data from registers, memory, or other components to be
  //   ----- DR AS SOURCE -----
  //   ----- MEMORY AS SOURCE -----
endmodule

module ALU_SELECT (
  input  IFF,
  input  B9,
  input  D5,
  input  T5,
  input  D6,
  input  D7,
  input  T3,
  input  D1,
  input  D2,
  input  D0,
  output ALU_S0,
  output ALU_S1,
  output ALU_S2
);

  wire A1, A2, A3, A5, A6, A7, not_1_out, r;

  and and_1 (A1, D0, T5);
  and and_2 (A2, D1, T5);
  and and_3 (A3, D2, T5);
  not not_1 (not_1_out, IFF);
  or or_1 (ALU_S0, A1, A3, A5, A7);
  or or_2 (ALU_S1, A2, A3, A6, A7);
  or or_3 (ALU_S2, 1'b0, A5, A6, A7);
  and and_4 (r, T3, not_1_out, D7);
  and and_5 (A5, r, B9);
  and and_6 (A7, r, D6);
  and and_7 (A6, r, D5);

  // Other names for the same wires on the sheet: B6 = D6; B7 = D5; I = IFF; rB6 = A7; rB7 = A6; rB9 = A5

  // Notes on the sheet:
  //   USE - 
  //   AND
  //   ADD
  //   DR
  //   INPR
  //   CMA
  //   SHR
  //   SHL
  //   ALU SELECTION SUBCIRCUIT
  //   cycle, allowing for smooth execution of operations within the CPU.
  //   This sub-circuit generates selection variables for the ALU based on the timing signal playing a crucial role
  //   that determine which specific operation the ALU should perform, such as addition, subtraction, logical
  //   operations, or other arithmetic functions. These variables are generated by the sub-circuit based on the
  //   in controlling the operation of the Arithmetic Logic Unit (ALU). The selection variables act as control signals
  //   timing signal, which synchronizes the operation of the ALU with the overall system. By using timing signals,
  //   the sub-circuit ensures that the ALU performs the correct operation at the right moment in the instruction
endmodule

module Data_Line (
  input  MX_S0,
  input  MX_S1,
  input  MX_S2,
  input  [15:0] MEM_OUT,
  input  AR_INC,
  input  AR_LOAD,
  input  AR_CLEAR,
  input  PC_INC,
  input  PC_LOAD,
  input  PC_CLEAR,
  input  E_COMP,
  input  E_CLR,
  input  DR_INC,
  input  DR_LOAD,
  input  E_LOAD,
  input  DR_CLEAR,
  input  AC_INC,
  input  AC_LOAD,
  input  AC_CLEAR,
  input  rB6,
  input  rB7,
  input  ADD,
  input  ALU_S0,
  input  ALU_S1,
  input  ALU_S2,
  input  IR_LOAD,
  input  TR_INC,
  input  TR_LOAD,
  input  TR_CLEAR,
  input  OP_LOAD,
  input  CLK,
  output [11:0] ADDRESS,
  output [15:0] MEM_IN,
  output [15:0] AR_OP,
  output [15:0] PC_OP,
  output E_op,
  output [15:0] DR_OP,
  output [15:0] AC_OP,
  output [15:0] INR_OP,
  output [15:0] IR_OP,
  output [15:0] TR_OP,
  output [15:0] OPR_OP
);

  wire alu_16bit_1_alu_0, alu_16bit_1_alu_15, alu_16bit_1_cout, multiplexer_1_out, multiplexer_2_out,
       multiplexer_3_out;
  wire [15:0] alu_16bit_1_op;

  Multiplexer multiplexer_1 (.in0(E_op), .in1(alu_16bit_1_alu_15), .out(multiplexer_1_out), .sel(rB6));
  Multiplexer multiplexer_2 (.in0(multiplexer_1_out), .in1(alu_16bit_1_alu_0), .out(multiplexer_2_out), .sel(rB7));
  Multiplexer multiplexer_3 (.in0(multiplexer_2_out), .in1(alu_16bit_1_cout), .out(multiplexer_3_out), .sel(ADD));
  E_FF e_ff_1 (.CMP(E_COMP), .CLR(E_CLR), .INP(multiplexer_3_out), .Load(E_LOAD), .CLK(CLK), .OP(E_op));
  ALU_16bit alu_16bit_1 (
    .DR(DR_OP), .INPR(INR_OP), .AC(AC_OP), .S0(ALU_S0), .S1(ALU_S1), .S2(ALU_S2), .SHR(AC_OP), .SHL(AC_OP),
    .ALU_0(alu_16bit_1_alu_0), .Cout(alu_16bit_1_cout), .ALU_15(alu_16bit_1_alu_15), .OP(alu_16bit_1_op));
  AR ar_1 (
    .INC(AR_INC), .LOAD(AR_LOAD), .CLR(AR_CLEAR), .CLK(CLK), .New_data(MEM_IN), .Data_Out(AR_OP),
    .Address(ADDRESS));
  PC pc_1 (.INC(PC_INC), .LOAD(PC_LOAD), .CLR(PC_CLEAR), .CLK(CLK), .New_data(MEM_IN), .Data_Out(PC_OP));
  DR dr_1 (.INC(DR_INC), .LOAD(DR_LOAD), .CLR(DR_CLEAR), .CLK(CLK), .New_data(MEM_IN), .Data_Out(DR_OP));
  AC ac_1 (.INC(AC_INC), .LOAD(AC_LOAD), .CLR(AC_CLEAR), .CLK(CLK), .New_data(alu_16bit_1_op), .Data_Out(AC_OP));
  InputR inputr_1 (.CLK(CLK), .New_data(MEM_IN), .data_out(INR_OP));
  IR ir_1 (.LOAD(IR_LOAD), .CLK(CLK), .New_data(MEM_IN), .Data_Out(IR_OP));
  TR tr_1 (.INC(TR_INC), .LOAD(TR_LOAD), .CLR(TR_CLEAR), .CLK(CLK), .New_data(MEM_IN), .Data_Out(TR_OP));
  OutputR outputr_1 (.LOAD(OP_LOAD), .CLK(CLK), .New_data(MEM_IN), .data_out(OPR_OP));
  Multiplexer #(.select(3), .width(16)) multiplexer_4 (
    .in1(AR_OP), .in2(PC_OP), .in3(DR_OP), .in4(AC_OP), .in5(IR_OP), .in6(TR_OP), .in7(MEM_OUT),
    .out(MEM_IN), .sel({MX_S2, MX_S1, MX_S0}));  // open: in0

  // Notes on the sheet:
  //   USE - 
  //   COMMON DATA PATH
  //   and data manipulation.         
  //   Above Mux selects the required value to be entered 
  //   in E flip Flop according to the timing signal activated         
  //   execution. It routes data between registers like the Program Counter (PC), Instruction Register (IR), and
  //   The Common Data Path connects CPU registers and components enabling data transfer during instruction
  //   Accumulator (AC), ensuring proper data access and processing by the ALU. In the main circuit, memory will
  //   be integrated into this data path, allowing the CPU to read and write data, facilitating instruction fetching
endmodule

module AR (
  input  INC,
  input  LOAD,
  input  CLR,
  input  CLK,
  input  [15:0] New_data,
  output [15:0] Data_Out,
  output [11:0] Address
);

  wire [11:0] adder_1_out, multiplexer_1_out, multiplexer_2_out, multiplexer_3_out;

  Adder #(.width(12)) adder_1 (.a(Address), .b(12'h1), .out(adder_1_out));  // open: cin, cout
  Multiplexer #(.width(12)) multiplexer_1 (.in0(Address), .in1(adder_1_out), .out(multiplexer_1_out), .sel(INC));
  Multiplexer #(.width(12)) multiplexer_2 (
    .in0(multiplexer_1_out), .in1(New_data[11:0]), .out(multiplexer_2_out), .sel(LOAD));
  Register #(.width(12)) register_1 (.D(multiplexer_3_out), .clk(CLK), .Q(Address));  // open: en, clr
  Multiplexer #(.width(12)) multiplexer_3 (
    .in0(multiplexer_2_out), .in1({12{1'b0}}), .out(multiplexer_3_out), .sel(CLR));

  assign Data_Out = {4'b0000, Address};

  // Notes on the sheet:
  //   ADRESS REGISTER
  //   USE - 
  //    directing the CPU where to read or write during execution.         
  //   The Address Register (AR) holds the memory address of data or instructions, 
endmodule

module PC (
  input  INC,
  input  LOAD,
  input  CLR,
  input  CLK,
  input  [15:0] New_data,
  output [15:0] Data_Out
);

  wire [11:0] adder_1_out, multiplexer_1_out, multiplexer_2_out, multiplexer_3_out;

  Adder #(.width(12)) adder_1 (.a(Data_Out[11:0]), .b(12'h1), .out(adder_1_out));  // open: cin, cout
  Multiplexer #(.width(12)) multiplexer_1 (.in0(Data_Out[11:0]), .in1(adder_1_out), .out(multiplexer_1_out), .sel(INC));
  Multiplexer #(.width(12)) multiplexer_2 (
    .in0(multiplexer_1_out), .in1(New_data[11:0]), .out(multiplexer_2_out), .sel(LOAD));
  Multiplexer #(.width(12)) multiplexer_3 (
    .in0(multiplexer_2_out), .in1({12{1'b0}}), .out(multiplexer_3_out), .sel(CLR));
  Register #(.width(12)) register_1 (.D(multiplexer_3_out), .clk(CLK), .Q(Data_Out[11:0]));  // open: en, clr

  assign Data_Out[15:12] = 4'b0000;

  // Notes on the sheet:
  //   USE - 
  //   PROGRAM COUNTER
  //   The Program Counter (PC) holds the address of the next instruction to be executed,
  //   ensuring the CPU fetches instructions in the correct sequence.         
endmodule

module DR (
  input  INC,
  input  LOAD,
  input  CLR,
  input  CLK,
  input  [15:0] New_data,
  output [15:0] Data_Out
);

  wire [15:0] adder_1_out, multiplexer_1_out, multiplexer_2_out, multiplexer_3_out;

  Adder #(.width(16)) adder_1 (.a(Data_Out), .b(16'h1), .out(adder_1_out));  // open: cin, cout
  Multiplexer #(.width(16)) multiplexer_1 (.in0(Data_Out), .in1(adder_1_out), .out(multiplexer_1_out), .sel(INC));
  Multiplexer #(.width(16)) multiplexer_2 (
    .in0(multiplexer_1_out), .in1(New_data), .out(multiplexer_2_out), .sel(LOAD));
  Register #(.width(16)) register_1 (.D(multiplexer_3_out), .clk(CLK), .Q(Data_Out));  // open: en, clr
  Multiplexer #(.width(16)) multiplexer_3 (
    .in0(multiplexer_2_out), .in1({16{1'b0}}), .out(multiplexer_3_out), .sel(CLR));

  // Notes on the sheet:
  //   DATA REGISTER
  //   USE - 
  //   The Data Register (DR) temporarily holds data read from or written to memory during CPU operations.
endmodule

module AC (
  input  INC,
  input  LOAD,
  input  CLR,
  input  CLK,
  input  [15:0] New_data,
  output [15:0] Data_Out
);

  wire [15:0] adder_1_out, multiplexer_1_out, multiplexer_2_out, multiplexer_3_out;

  Adder #(.width(16)) adder_1 (.a(Data_Out), .b(16'h1), .out(adder_1_out));  // open: cin, cout
  Multiplexer #(.width(16)) multiplexer_1 (.in0(Data_Out), .in1(adder_1_out), .out(multiplexer_1_out), .sel(INC));
  Multiplexer #(.width(16)) multiplexer_2 (
    .in0(multiplexer_1_out), .in1(New_data), .out(multiplexer_2_out), .sel(LOAD));
  Register #(.width(16)) register_1 (.D(multiplexer_3_out), .clk(CLK), .Q(Data_Out));  // open: en, clr
  Multiplexer #(.width(16)) multiplexer_3 (
    .in0(multiplexer_2_out), .in1({16{1'b0}}), .out(multiplexer_3_out), .sel(CLR));

  // Notes on the sheet:
  //   USE - 
  //   ACCUMULATOR
  //   The Accumulator (AC) is used to store intermediate results of arithmetic and logic operations performed by the CPU.
endmodule

module IR (
  input  LOAD,
  input  CLK,
  input  [15:0] New_data,
  output [15:0] Data_Out
);

  wire [15:0] multiplexer_1_out;

  Multiplexer #(.width(16)) multiplexer_1 (.in0(Data_Out), .in1(New_data), .out(multiplexer_1_out), .sel(LOAD));
  Register #(.width(16)) register_1 (.D(multiplexer_1_out), .clk(CLK), .Q(Data_Out));  // open: en, clr

  // Notes on the sheet:
  //   USE - 
  //   INSTRUCTION REGISTER
  //   which is then decoded and executed by the CPU.         
  //   The Instruction Register (IR) holds the current instruction fetched from memory, 
endmodule

module TR (
  input  INC,
  input  LOAD,
  input  CLR,
  input  CLK,
  input  [15:0] New_data,
  output [15:0] Data_Out
);

  wire [15:0] adder_1_out, multiplexer_1_out, multiplexer_2_out, multiplexer_3_out;

  Adder #(.width(16)) adder_1 (.a(Data_Out), .b(16'h1), .out(adder_1_out));  // open: cin, cout
  Multiplexer #(.width(16)) multiplexer_1 (.in0(Data_Out), .in1(adder_1_out), .out(multiplexer_1_out), .sel(INC));
  Multiplexer #(.width(16)) multiplexer_2 (
    .in0(multiplexer_1_out), .in1(New_data), .out(multiplexer_2_out), .sel(LOAD));
  Multiplexer #(.width(16)) multiplexer_3 (
    .in0(multiplexer_2_out), .in1({16{1'b0}}), .out(multiplexer_3_out), .sel(CLR));
  Register #(.width(16)) register_1 (.D(multiplexer_3_out), .clk(CLK), .Q(Data_Out));  // open: en, clr

  // Notes on the sheet:
  //   USE - 
  //   NOTE - 
  //   TEMPORARY REGISTER
  //   or data transfer within the CPU.
  //   USED IN INTERRUPTS ONLY!
  //   The Temporary Register (TR) is used to hold intermediate data temporarily during instruction execution 
endmodule

module InputR (
  input  CLK,
  input  [15:0] New_data,
  output [15:0] data_out
);

  Register register_1 (.D(New_data[7:0]), .clk(CLK), .Q(data_out[7:0]));  // open: en, clr

  assign data_out[15:8] = {8{1'b0}};

  // Notes on the sheet:
  //   INPUT REGISTER
  //   USE - 
  //   NOTE - 
  //   USED IN I/O OPERATION ONLY!
  //   The Input Register holds data received from an input device before it is processed by the CPU
endmodule

module OutputR (
  input  LOAD,
  input  CLK,
  input  [15:0] New_data,
  output [15:0] data_out
);

  wire [7:0] multiplexer_1_out;

  Multiplexer #(.width(8)) multiplexer_1 (
    .in0(data_out[7:0]), .in1(New_data[7:0]), .out(multiplexer_1_out), .sel(LOAD));
  Register register_1 (.D(multiplexer_1_out), .clk(CLK), .Q(data_out[7:0]));  // open: en, clr

  assign data_out[15:8] = {8{1'b0}};

  // Notes on the sheet:
  //   USE - 
  //   NOTE - 
  //   OUTPUT REGISTER
  //   USED IN I/O OPERATION ONLY!
  //   Output Register holds data from the CPU that is to be sent to an output device.
endmodule
